// Logisim project 8_bit_registers.circ as structural Verilog: 1 circuit, main circuit main
module main (
);

  wire and_1_out, and_2_out, and_3_out, and_4_out, and_5_out, and_6_out, and_7_out, and_8_out, and_9_out,
       and_10_out, and_11_out, and_12_out, and_13_out, and_14_out, and_15_out, and_16_out, and_17_out,
       and_18_out, and_19_out, and_20_out, and_21_out, and_22_out, and_23_out, and_24_out, and_25_out,
       and_26_out, and_27_out, and_28_out, and_29_out, and_30_out, and_31_out, and_32_out, button_1_out,
       dipswitch_1_sw1, dipswitch_1_sw2, dipswitch_1_sw3, dipswitch_1_sw4, dipswitch_1_sw5, dipswitch_1_sw6,
       dipswitch_1_sw7, dipswitch_1_sw8, n7408_1_pin4, n7408_1_pin6, n7408_1_pin11, n7408_1_pin12, nor_1_out,
       nor_2_out, nor_3_out, nor_4_out, nor_5_out, nor_6_out, nor_7_out, nor_8_out, nor_9_out, nor_10_out,
       nor_11_out, nor_12_out, nor_13_out, nor_14_out, nor_15_out, nor_16_out, nor_17_out, nor_18_out,
       nor_19_out, nor_20_out, nor_21_out, nor_22_out, nor_23_out, nor_24_out, nor_25_out, nor_26_out,
       nor_27_out, nor_28_out, nor_29_out, nor_30_out, nor_31_out, nor_32_out, not_1_out, not_2_out,
       not_3_out, not_4_out, not_5_out, not_6_out, not_7_out, not_8_out, not_9_out, not_10_out, not_11_out,
       not_12_out, not_13_out, not_14_out, not_15_out, not_16_out;

  not not_1 (not_1_out, dipswitch_1_sw1);
  not not_2 (not_2_out, dipswitch_1_sw2);
  not not_3 (not_3_out, dipswitch_1_sw3);
  not not_4 (not_4_out, dipswitch_1_sw4);
  not not_5 (not_5_out, dipswitch_1_sw8);
  not not_6 (not_6_out, dipswitch_1_sw7);
  not not_7 (not_7_out, dipswitch_1_sw6);
  not not_8 (not_8_out, dipswitch_1_sw5);
  and and_1 (and_1_out, dipswitch_1_sw1, n7408_1_pin11);
  and and_2 (and_2_out, n7408_1_pin11, not_1_out);
  and and_3 (and_3_out, dipswitch_1_sw2, n7408_1_pin11);
  and and_4 (and_4_out, n7408_1_pin11, not_2_out);
  and and_5 (and_5_out, dipswitch_1_sw3, n7408_1_pin11);
  and and_6 (and_6_out, n7408_1_pin11, not_3_out);
  and and_7 (and_7_out, dipswitch_1_sw4, n7408_1_pin11);
  and and_8 (and_8_out, n7408_1_pin11, not_4_out);
  and and_9 (and_9_out, dipswitch_1_sw8, n7408_1_pin11);
  and and_10 (and_10_out, n7408_1_pin11, not_5_out);
  and and_11 (and_11_out, dipswitch_1_sw7, n7408_1_pin11);
  and and_12 (and_12_out, n7408_1_pin11, not_6_out);
  and and_13 (and_13_out, dipswitch_1_sw6, n7408_1_pin11);
  and and_14 (and_14_out, n7408_1_pin11, not_7_out);
  and and_15 (and_15_out, dipswitch_1_sw5, n7408_1_pin11);
  and and_16 (and_16_out, n7408_1_pin11, not_8_out);
  LedBar ledbar_1 (
    .led0(nor_1_out), .led1(nor_2_out), .led2(nor_3_out), .led3(nor_4_out), .led4(nor_8_out),
    .led5(nor_7_out), .led6(nor_6_out), .led7(nor_5_out));
  nor nor_1 (nor_1_out, nor_9_out, and_2_out);
  nor nor_2 (nor_2_out, nor_10_out, and_4_out);
  nor nor_3 (nor_3_out, nor_11_out, and_6_out);
  nor nor_4 (nor_4_out, nor_12_out, and_8_out);
  nor nor_5 (nor_5_out, nor_13_out, and_10_out);
  nor nor_6 (nor_6_out, nor_14_out, and_12_out);
  nor nor_7 (nor_7_out, nor_15_out, and_14_out);
  nor nor_8 (nor_8_out, nor_16_out, and_16_out);
  Button button_1 (.out(button_1_out));
  _7408 u_7408_1 (
    .pin1(nor_5_out), .pin2(nor_5_out), .pin4(n7408_1_pin4), .pin5(button_1_out), .pin6(n7408_1_pin6),
    .pin13(button_1_out), .pin12(n7408_1_pin12), .pin11(n7408_1_pin11));  // open: pin3, pin10, pin9, pin8
  nor nor_9 (nor_9_out, and_1_out, nor_1_out);
  nor nor_10 (nor_10_out, and_3_out, nor_2_out);
  nor nor_11 (nor_11_out, and_5_out, nor_3_out);
  nor nor_12 (nor_12_out, and_7_out, nor_4_out);
  nor nor_13 (nor_13_out, and_9_out, nor_5_out);
  nor nor_14 (nor_14_out, and_11_out, nor_6_out);
  nor nor_15 (nor_15_out, and_13_out, nor_7_out);
  nor nor_16 (nor_16_out, and_15_out, nor_8_out);
  DipSwitch #(.number(10)) dipswitch_1 (
    .sw1(dipswitch_1_sw1), .sw2(dipswitch_1_sw2), .sw3(dipswitch_1_sw3), .sw4(dipswitch_1_sw4),
    .sw5(dipswitch_1_sw5), .sw6(dipswitch_1_sw6), .sw7(dipswitch_1_sw7), .sw8(dipswitch_1_sw8),
    .sw9(n7408_1_pin12), .sw10(n7408_1_pin4));
  LedBar ledbar_2 (
    .led0(nor_17_out), .led1(nor_18_out), .led2(nor_19_out), .led3(nor_20_out), .led4(nor_24_out),
    .led5(nor_23_out), .led6(nor_22_out), .led7(nor_21_out));
  not not_9 (not_9_out, dipswitch_1_sw1);
  not not_10 (not_10_out, dipswitch_1_sw2);
  not not_11 (not_11_out, dipswitch_1_sw3);
  not not_12 (not_12_out, dipswitch_1_sw4);
  not not_13 (not_13_out, dipswitch_1_sw8);
  not not_14 (not_14_out, dipswitch_1_sw7);
  not not_15 (not_15_out, dipswitch_1_sw6);
  not not_16 (not_16_out, dipswitch_1_sw5);
  and and_17 (and_17_out, dipswitch_1_sw1, n7408_1_pin6);
  and and_18 (and_18_out, n7408_1_pin6, not_9_out);
  and and_19 (and_19_out, dipswitch_1_sw2, n7408_1_pin6);
  and and_20 (and_20_out, n7408_1_pin6, not_10_out);
  and and_21 (and_21_out, dipswitch_1_sw3, n7408_1_pin6);
  and and_22 (and_22_out, n7408_1_pin6, not_11_out);
  and and_23 (and_23_out, dipswitch_1_sw4, n7408_1_pin6);
  and and_24 (and_24_out, n7408_1_pin6, not_12_out);
  and and_25 (and_25_out, dipswitch_1_sw8, n7408_1_pin6);
  and and_26 (and_26_out, n7408_1_pin6, not_13_out);
  and and_27 (and_27_out, dipswitch_1_sw7, n7408_1_pin6);
  and and_28 (and_28_out, n7408_1_pin6, not_14_out);
  and and_29 (and_29_out, dipswitch_1_sw6, n7408_1_pin6);
  and and_30 (and_30_out, n7408_1_pin6, not_15_out);
  and and_31 (and_31_out, dipswitch_1_sw5, n7408_1_pin6);
  and and_32 (and_32_out, n7408_1_pin6, not_16_out);
  nor nor_17 (nor_17_out, nor_25_out, and_18_out);
  nor nor_18 (nor_18_out, nor_26_out, and_20_out);
  nor nor_19 (nor_19_out, nor_27_out, and_22_out);
  nor nor_20 (nor_20_out, nor_28_out, and_24_out);
  nor nor_21 (nor_21_out, nor_29_out, and_26_out);
  nor nor_22 (nor_22_out, nor_30_out, and_28_out);
  nor nor_23 (nor_23_out, nor_31_out, and_30_out);
  nor nor_24 (nor_24_out, nor_32_out, and_32_out);
  nor nor_25 (nor_25_out, and_17_out, nor_17_out);
  nor nor_26 (nor_26_out, and_19_out, nor_18_out);
  nor nor_27 (nor_27_out, and_21_out, nor_19_out);
  nor nor_28 (nor_28_out, and_23_out, nor_20_out);
  nor nor_29 (nor_29_out, and_25_out, nor_21_out);
  nor nor_30 (nor_30_out, and_27_out, nor_22_out);
  nor nor_31 (nor_31_out, and_29_out, nor_23_out);
  nor nor_32 (nor_32_out, and_31_out, nor_24_out);
endmodule
